// Logisim project circuito.circ as structural Verilog: 1 circuit, main circuit Circuito
module Circuito (
  input  READY,
  input  C3,
  input  C2,
  input  C1,
  input  C0,
  input  D1,
  input  D0
);

  wire A_out, and_1_out, and_2_out, and_3_out, and_4_out, and_5_out, and_6_out, and_7_out, and_8_out,
       and_9_out, and_10_out, B_out, C_out, D_out, E_out, F_out, G_out, not_1_out, not_2_out, not_3_out,
       not_4_out, not_5_out, S0_out, S1_out;

  not not_1 (not_1_out, D0);
  not not_2 (not_2_out, D1);
  not not_3 (not_3_out, C2);
  not not_4 (not_4_out, C3);
  not not_5 (not_5_out, C1);
  and and_1 (and_1_out, C1, C2, ~C3);  // AND_Gate
  and and_2 (and_2_out, not_1_out, not_2_out);
  and and_3 (and_3_out, C2, C3);
  and and_4 (and_4_out, not_3_out, not_4_out, D1);
  and and_5 (and_5_out, not_5_out, C2, D1);
  and and_6 (and_6_out, C0, C1, C3);
  or S1 (S1_out, ~D1, C3, and_1_out);  // OR_Gate
  or S0 (S0_out, and_2_out, and_3_out, and_4_out, and_5_out, and_6_out);
  and and_7 (and_7_out, READY, S1_out);
  and and_8 (and_8_out, READY, ~S0_out);  // AND_Gate
  and and_9 (and_9_out, READY, S0_out);
  and and_10 (and_10_out, READY, ~S0_out, ~S1_out);  // AND_Gate
  or A (A_out, and_7_out, and_8_out);
  or B (B_out, and_7_out, and_9_out);
  or C (C_out, and_9_out, 1'b0);
  or D (D_out, and_7_out, and_8_out);
  or E (E_out, and_8_out, 1'b0);
  or F (F_out, and_10_out, 1'b0);
  or G (G_out, and_7_out, and_8_out);
  _7_Segment_Display u_7_segment_display_1 (
    .g(G_out), .f(F_out), .a(A_out), .b(B_out), .e(E_out), .d(D_out), .c(C_out));  // open: dp
endmodule
