// Logisim project circuitologisim copy.circ as structural Verilog: 1 circuit, main circuit main
// 3
module main (
  input  C3,
  input  RESET,
  input  READY,
  input  C2,
  input  C1,
  input  C0,
  input  D1,
  input  D0
);

  wire A_out, and_1_out, and_2_out, and_3_out, and_4_out, and_5_out, and_6_out, and_7_out, and_8_out,
       and_9_out, and_10_out, and_11_out, and_12_out, and_13_out, and_14_out, and_15_out, and_16_out,
       and_17_out, and_18_out, and_19_out, and_20_out, and_21_out, and_22_out, and_23_out, and_24_out,
       and_25_out, and_26_out, B_out, C_out, D_out, E_out, F_out, G_out, S0_out, S1_out;

  and and_1 (and_1_out, C3, C2);
  and and_2 (and_2_out, C3, ~D0, D1);  // AND_Gate
  and and_3 (and_3_out, C1, C2, ~C3, ~D0, D1);  // AND_Gate
  and and_4 (and_4_out, C3, C2);
  and and_5 (and_5_out, ~D1, ~D0);  // AND_Gate
  and and_6 (and_6_out, C1, C3, C0);
  and and_7 (and_7_out, ~C3, ~C2, D1);  // AND_Gate
  and and_8 (and_8_out, C0, C1, C3);
  or S1 (S1_out, and_3_out, and_1_out, and_6_out, and_2_out, ~D1);  // OR_Gate
  and and_9 (and_9_out, ~C1, D1, C2);  // AND_Gate
  or S0 (S0_out, and_9_out, and_5_out, and_7_out, and_4_out, and_8_out);
  and and_10 (and_10_out, ~READY, RESET);  // AND_Gate
  and and_11 (and_11_out, READY, S1_out);
  and and_12 (and_12_out, READY, ~S0_out);  // AND_Gate
  and and_13 (and_13_out, ~READY, RESET);  // AND_Gate
  and and_14 (and_14_out, READY, S0_out);
  and and_15 (and_15_out, READY, S1_out);
  and and_16 (and_16_out, ~READY, RESET);  // AND_Gate
  and and_17 (and_17_out, READY, S0_out);
  and and_18 (and_18_out, ~READY, RESET);  // AND_Gate
  and and_19 (and_19_out, READY, S1_out);
  and and_20 (and_20_out, READY, ~S0_out);  // AND_Gate
  and and_21 (and_21_out, ~READY, RESET);  // AND_Gate
  and and_22 (and_22_out, READY, ~S0_out);  // AND_Gate
  and and_23 (and_23_out, ~READY, RESET);  // AND_Gate
  and and_24 (and_24_out, READY, ~S0_out, ~S1_out);  // AND_Gate
  and and_25 (and_25_out, READY, S1_out);
  and and_26 (and_26_out, READY, ~S0_out);  // AND_Gate
  or A (A_out, and_10_out, and_11_out, and_12_out);
  or B (B_out, and_13_out, and_14_out, and_15_out);
  or C (C_out, and_16_out, and_17_out);
  or D (D_out, and_18_out, and_19_out, and_20_out);
  or E (E_out, and_21_out, and_22_out);
  or F (F_out, and_23_out, and_24_out);
  or G (G_out, and_25_out, and_26_out);
  _7_Segment_Display u_7_segment_display_1 (
    .g(G_out), .f(F_out), .a(A_out), .b(B_out), .e(E_out), .d(D_out), .c(C_out));  // open: dp
endmodule
